# Fritzing sketch led_rgb (saved by Fritzing 0.8.7b)
breadboards: 1

parts:
  Componente1 = Arduino Uno (Rev3)
  R1 = Resistor [tolerance=±5% resistance=200 package=THT]
  LED1 = RGB LED (com. anode, rbg) [package="5 mm [THT]"]
  R2 = Resistor [tolerance=±5% resistance=200 package=THT]
  R3 = Resistor [tolerance=±5% resistance=200 package=THT]

nets:
  N1: Componente1.D9_PWM, R3.Pin_1
  N2: Componente1.D10_PWM/SS, R2.Pin_1
  N3: Componente1.D11_PWM/MOSI, R1.Pin_1
  N4: Componente1.GND, LED1.common_anode
  N5: R1.Pin_0, LED1.red_cathode
  N6: LED1.blue_cathode, R2.Pin_0
  N7: LED1.green_cathode, R3.Pin_0
