# Fritzing sketch blink_supercar (saved by Fritzing 0.8.7b)
breadboards: 1

parts:
  Componente1 = Arduino Uno (Rev3)
  LED1 = LED - 5mm [color="Red (633nm)" package="5 mm [THT]"]
  R1 = Resistor [tolerance=±5% resistance=200 package=THT]
  LED2 = LED - 5mm [color="Red (633nm)" package="5 mm [THT]"]
  LED3 = LED - 5mm [color="Red (633nm)" package="5 mm [THT]"]
  LED4 = LED - 5mm [color="Red (633nm)" package="5 mm [THT]"]
  R2 = Resistor [tolerance=±5% resistance=200 package=THT]
  R3 = Resistor [tolerance=±5% resistance=200 package=THT]
  R4 = Resistor [tolerance=±5% resistance=200 package=THT]

nets:
  N1: Componente1.D9_PWM, R3.Pin_1
  N2: Componente1.D10_PWM/SS, R2.Pin_1
  N3: Componente1.D11_PWM/MOSI, R1.Pin_1
  N4: Componente1.GND, LED1.cathode, LED2.cathode, LED3.cathode, LED4.cathode
  N5: Componente1.D6_PWM, R4.Pin_1
  N6: LED1.anode, R1.Pin_0
  N7: LED2.anode, R2.Pin_0
  N8: LED3.anode, R3.Pin_0
  N9: LED4.anode, R4.Pin_0
