# Fritzing sketch a_bottone_a_pressione (saved by Fritzing 0.8.7b)
breadboards: 1

parts:
  Componente1 = Arduino Uno (Rev3)
  R3 = Resistor [tolerance=±5% resistance=200 package=THT]
  LED1 = LED - 5mm [color="Red (633nm)" package="5 mm [THT]"]
  S1 = Pushbutton [package="[THT]"]
  R4 = Resistor [tolerance=±5% resistance=200 package=THT]

nets:
  N1: Componente1.D9_PWM, R3.Pin_1
  N2: Componente1.GND, LED1.cathode, S1.Pin_3, S1.Pin_4, R4.Pin_1
  N3: Componente1.D2, S1.Pin_1, S1.Pin_2, R4.Pin_0
  N4: R3.Pin_0, LED1.anode
