# Fritzing sketch c_fotoresistenza (saved by Fritzing 0.8.7b)
breadboards: 1

parts:
  Componente1 = Arduino Uno (Rev3)
  R3 = Resistor [tolerance=±5% resistance=200 package=THT]
  LED1 = LED - 5mm [color="Red (633nm)" package="5 mm [THT]"]
  R5 = Photocell (LDR) [package=THT]
  R6 = Resistor [tolerance=±5% resistance=200 package=THT]

nets:
  N1: Componente1.A0, R5.pin_1, R6.Pin_0
  N2: Componente1.D9_PWM, R3.Pin_1
  N3: Componente1.GND, LED1.cathode, R5.pin_0, R6.Pin_1
  N4: R3.Pin_0, LED1.anode
