# Fritzing sketch a_motorDC_transistor_PWM_02 (saved by Fritzing 0.8.7b)
breadboards: 1

parts:
  Componente1 = Arduino Uno (Rev3)
  M1 = DC Motor
  D1 = Rectifier Diode [part_number=1N4001 package="300 mil [THT]"]
  Q1 = Basic FET P-Channel [package="TO220 [THT]"]
  R1 = Resistor [tolerance=±5% resistance=220 package=THT]
  R2 = Rotary Potentiometer (Small) [maximum_resistance=100kΩ package=THT]

nets:
  N1: Componente1.A0, R2.wiper
  N2: Componente1.D9_PWM, R1.Pin_0
  N3: Componente1.5V, Q1.drain, R2.leg2
  N4: Componente1.GND, M1.pin_2, D1.anode, R2.leg1
  N5: M1.pin_1, D1.cathode, Q1.source
  N6: Q1.gate, R1.Pin_1
