# Fritzing sketch a_motorDC_transistor_PWM_03 (saved by Fritzing 0.8.7b)
breadboards: 1

parts:
  M1 = DC Motor
  Componente1 = Arduino Uno (Rev3)
  R1 = Resistor [tolerance=±5% resistance=220 package=THT]
  R2 = Rotary Potentiometer (Small) [maximum_resistance=100kΩ package=THT]
  D1 = Rectifier Diode [part_number=1N4001 package="300 mil [THT]"]
  Q1 = Basic FET P-Channel [package="TO220 [THT]"]
  VCC1 = Battery

nets:
  N1: M1.pin_1, D1.cathode, Q1.source
  N2: M1.pin_2, Componente1.GND, R2.leg1, D1.anode, VCC1.-
  N3: Componente1.A0, R2.wiper
  N4: Componente1.D9_PWM, R1.Pin_0
  N5: R1.Pin_1, Q1.gate
  N6: R2.leg2, Q1.drain, VCC1.+
